// Logisim project Lab4_Backup.circ as structural Verilog: 7 circuits, main circuit main
module main (
  input  [19:0] Instruction
);

  wire alu_control_1_alu_src, undriven, undriven_2;
  wire [3:0] alu_control_1_alu_ctrl0;
  wire [31:0] alu32_1_result, multiplexer_1_out, register_file_1_rdata, register_file_1_rdata2;
  wire [31:5] undriven_3;

  register_file register_file_1 (
    .WData(alu32_1_result), .RReg1(Instruction[9:5]), .Clock_in(undriven_2), .WReg(Instruction[19:15]),
    .Write(undriven), .RReg2(Instruction[14:10]), .RData(register_file_1_rdata),
    .RData2(register_file_1_rdata2));
  ALU_control alu_control_1 (
    .I30(Instruction[0]), .I14(Instruction[1]), .I13(Instruction[2]), .I12(Instruction[3]),
    .I6(Instruction[4]), .I5(Instruction[5]), .I4(Instruction[6]), .ALU_CTRL3(alu_control_1_alu_ctrl0[3]),
    .ALU_CTRL2(alu_control_1_alu_ctrl0[2]), .ALU_CTRL1(alu_control_1_alu_ctrl0[1]),
    .ALU_CTRL0(alu_control_1_alu_ctrl0[0]), .ALU_SRC(alu_control_1_alu_src));
  Multiplexer #(.enable("false"), .width(32)) multiplexer_1 (
    .in0(register_file_1_rdata2), .in1({undriven_3, Instruction[4:0]}), .out(multiplexer_1_out),
    .sel(alu_control_1_alu_src));
  ALU32 alu32_1 (
    .ALU_Ctrl(alu_control_1_alu_ctrl0), .A(register_file_1_rdata), .B(multiplexer_1_out),
    .Result(alu32_1_result));  // open: C_in, C_out
  // Pins of 5 and 7 and 20 bits meet at Instruction
  // Pins of 5 and 32 bits meet at {undriven_3, Instruction[4:0]}
endmodule

module FullAdder (
  input  A,
  input  B,
  input  C_in,
  output S,
  output out_5
);

  wire and_1_out, and_2_out, xor_1_out;

  xor xor_1 (xor_1_out, A, B);
  and and_1 (and_1_out, A, B);
  xor xor_2 (S, xor_1_out, C_in);
  and and_2 (and_2_out, xor_1_out, C_in);
  or or_1 (out_5, and_2_out, and_1_out);
endmodule

module ALU (
  input  [3:0] ALU_Ctrl,
  input  A,
  input  B,
  input  C_in,
  output R,
  output C_out
);

  wire and_1_out, fulladder_1_s, multiplexer_1_out, not_1_out, or_1_out, xor_1_out;

  not not_1 (not_1_out, B);
  Multiplexer #(.enable("false")) multiplexer_1 (.in0(B), .in1(not_1_out), .out(multiplexer_1_out), .sel(ALU_Ctrl[2]));
  and and_1 (and_1_out, A, multiplexer_1_out);
  or or_1 (or_1_out, A, multiplexer_1_out);
  xor xor_1 (xor_1_out, A, multiplexer_1_out);
  FullAdder fulladder_1 (.A(A), .B(multiplexer_1_out), .C_in(C_in), .S(fulladder_1_s), .out_5(C_out));
  Multiplexer #(.enable("false"), .select(2)) multiplexer_2 (
    .in0(and_1_out), .in1(or_1_out), .in2(xor_1_out), .in3(fulladder_1_s), .out(R), .sel(ALU_Ctrl[1:0]));
endmodule

module ALU4 (
  input  [3:0] ALU_Ctrl,
  input  C_in,
  input  [3:0] A,
  input  [3:0] B,
  output [3:0] S,
  output C_out
);

  wire alu_1_c_out, alu_2_c_out, alu_3_c_out;

  ALU alu_1 (.ALU_Ctrl(ALU_Ctrl), .A(A[0]), .B(B[0]), .C_in(C_in), .R(S[0]), .C_out(alu_1_c_out));
  ALU alu_2 (.ALU_Ctrl(ALU_Ctrl), .A(A[1]), .B(B[1]), .C_in(alu_1_c_out), .R(S[1]), .C_out(alu_2_c_out));
  ALU alu_3 (.ALU_Ctrl(ALU_Ctrl), .A(A[2]), .B(B[2]), .C_in(alu_2_c_out), .R(S[2]), .C_out(alu_3_c_out));
  ALU alu_4 (.ALU_Ctrl(ALU_Ctrl), .A(A[3]), .B(B[3]), .C_in(alu_3_c_out), .R(S[3]), .C_out(C_out));
endmodule

module ALU32 (
  input  [3:0] ALU_Ctrl,
  input  C_in,
  input  [31:0] A,
  input  [31:0] B,
  output [31:0] Result,
  output C_out
);

  wire alu4_1_c_out, alu4_2_c_out, alu4_3_c_out, alu4_4_c_out, alu4_5_c_out, alu4_6_c_out, alu4_7_c_out;

  ALU4 alu4_1 (.ALU_Ctrl(ALU_Ctrl), .C_in(C_in), .A(A[3:0]), .B(B[3:0]), .S(Result[3:0]), .C_out(alu4_1_c_out));
  ALU4 alu4_2 (.ALU_Ctrl(ALU_Ctrl), .C_in(alu4_1_c_out), .A(A[7:4]), .B(B[7:4]), .S(Result[7:4]), .C_out(alu4_2_c_out));
  ALU4 alu4_3 (
    .ALU_Ctrl(ALU_Ctrl), .C_in(alu4_2_c_out), .A(A[11:8]), .B(B[11:8]), .S(Result[11:8]), .C_out(alu4_3_c_out));
  ALU4 alu4_4 (
    .ALU_Ctrl(ALU_Ctrl), .C_in(alu4_3_c_out), .A(A[15:12]), .B(B[15:12]), .S(Result[15:12]),
    .C_out(alu4_4_c_out));
  ALU4 alu4_5 (
    .ALU_Ctrl(ALU_Ctrl), .C_in(alu4_4_c_out), .A(A[19:16]), .B(B[19:16]), .S(Result[19:16]),
    .C_out(alu4_5_c_out));
  ALU4 alu4_6 (
    .ALU_Ctrl(ALU_Ctrl), .C_in(alu4_5_c_out), .A(A[23:20]), .B(B[23:20]), .S(Result[23:20]),
    .C_out(alu4_6_c_out));
  ALU4 alu4_7 (
    .ALU_Ctrl(ALU_Ctrl), .C_in(alu4_6_c_out), .A(A[27:24]), .B(B[27:24]), .S(Result[27:24]),
    .C_out(alu4_7_c_out));
  ALU4 alu4_8 (.ALU_Ctrl(ALU_Ctrl), .C_in(alu4_7_c_out), .A(A[31:28]), .B(B[31:28]), .S(Result[31:28]), .C_out(C_out));
endmodule

module ALU_control (
  input  I30,
  input  I14,
  input  I13,
  input  I12,
  input  I6,
  input  I5,
  input  I4,
  output ALU_CTRL3,
  output ALU_CTRL2,
  output ALU_CTRL1,
  output ALU_CTRL0,
  output ALU_SRC
);

  wire and_3_out, and_4_out, and_5_out, and_6_out, not_1_out, not_2_out, not_3_out, not_4_out, not_5_out,
       not_6_out;

  not not_1 (not_1_out, I30);
  not not_2 (not_2_out, I14);
  not not_3 (not_3_out, I13);
  not not_4 (not_4_out, I12);
  not not_5 (not_5_out, I5);
  not not_6 (not_6_out, I4);
  and and_1 (ALU_CTRL3, not_3_out, I12);
  and and_2 (ALU_CTRL2, I30, not_4_out, I5);
  and and_3 (and_3_out, not_2_out, not_4_out);
  and and_4 (and_4_out, not_2_out, not_4_out);
  and and_5 (and_5_out, I13, not_4_out);
  and and_6 (and_6_out, not_1_out, I14, I12, not_3_out);
  or or_1 (ALU_SRC, not_5_out, not_6_out);
  or or_2 (ALU_CTRL1, I30, not_6_out, and_3_out);
  or or_3 (ALU_CTRL0, and_4_out, and_5_out, and_6_out);
endmodule

module register_file (
  input  [31:0] WData,
  input  [4:0] RReg1,
  input  Clock_in,
  input  [4:0] WReg,
  input  Write,
  input  [4:0] RReg2,
  output [31:0] RData,
  output [31:0] RData2
);

  wire t1, t2, t3, t4, t5, t6, t7, t8, t9, t10, t11, t12, t13, t14, t15, t16, t17, t18, t19, t20, t21, t22,
       t23, t24, t25, t26, t27, t28, t29, t30, t31, t32;
  wire [31:0] o1, o2, o3, o4, o5, o6, o7, o8, o9, o10, o11, o12, o13, o14, o15, o16, o17, o18, o19, o20, o21,
       o22, o23, o24, o25, o26, o27, o28, o29, o30, o31, o32;

  Demultiplexer #(.enable("false"), .select(5)) demultiplexer_1 (
    .out0(t1), .out1(t2), .out2(t3), .out3(t4), .out4(t5), .out5(t6), .out6(t7), .out7(t8), .out8(t9),
    .out9(t10), .out10(t11), .out11(t12), .out12(t13), .out13(t14), .out14(t15), .out15(t16), .out16(t17),
    .out17(t18), .out18(t19), .out19(t20), .out20(t21), .out21(t22), .out22(t23), .out23(t24), .out24(t25),
    .out25(t26), .out26(t27), .out27(t28), .out28(t29), .out29(t30), .out30(t31), .out31(t32), .in(Write),
    .sel(WReg));
  Register #(.width(32)) register_1 (.D(WData), .en(t1), .clk(Clock_in), .Q(o1), .clr(Write));
  Register #(.width(32)) register_2 (.D(WData), .en(t2), .clk(Clock_in), .Q(o2));  // open: clr
  Register #(.width(32)) register_3 (.D(WData), .en(t3), .clk(Clock_in), .Q(o3));  // open: clr
  Register #(.width(32)) register_4 (.D(WData), .en(t4), .clk(Clock_in), .Q(o4));  // open: clr
  Register #(.width(32)) register_5 (.D(WData), .en(t5), .clk(Clock_in), .Q(o5));  // open: clr
  Register #(.width(32)) register_6 (.D(WData), .en(t6), .clk(Clock_in), .Q(o6));  // open: clr
  Register #(.width(32)) register_7 (.D(WData), .en(t7), .clk(Clock_in), .Q(o7));  // open: clr
  Register #(.width(32)) register_8 (.D(WData), .en(t8), .clk(Clock_in), .Q(o8));  // open: clr
  Register #(.width(32)) register_9 (.D(WData), .en(t9), .clk(Clock_in), .Q(o9));  // open: clr
  Register #(.width(32)) register_10 (.D(WData), .en(t10), .clk(Clock_in), .Q(o10));  // open: clr
  Register #(.width(32)) register_11 (.D(WData), .en(t11), .clk(Clock_in), .Q(o11));  // open: clr
  Register #(.width(32)) register_12 (.D(WData), .en(t12), .clk(Clock_in), .Q(o12));  // open: clr
  Register #(.width(32)) register_13 (.D(WData), .en(t13), .clk(Clock_in), .Q(o13));  // open: clr
  Register #(.width(32)) register_14 (.D(WData), .en(t14), .clk(Clock_in), .Q(o14));  // open: clr
  Register #(.width(32)) register_15 (.D(WData), .en(t15), .clk(Clock_in), .Q(o15));  // open: clr
  Register #(.width(32)) register_16 (.D(WData), .en(t16), .clk(Clock_in), .Q(o16));  // open: clr
  Register #(.width(32)) register_17 (.D(WData), .en(t17), .clk(Clock_in), .Q(o17));  // open: clr
  Register #(.width(32)) register_18 (.D(WData), .en(t18), .clk(Clock_in), .Q(o18));  // open: clr
  Register #(.width(32)) register_19 (.D(WData), .en(t19), .clk(Clock_in), .Q(o19));  // open: clr
  Register #(.width(32)) register_20 (.D(WData), .en(t20), .clk(Clock_in), .Q(o20));  // open: clr
  Register #(.width(32)) register_21 (.D(WData), .en(t21), .clk(Clock_in), .Q(o21));  // open: clr
  Register #(.width(32)) register_22 (.D(WData), .en(t22), .clk(Clock_in), .Q(o22));  // open: clr
  Register #(.width(32)) register_23 (.D(WData), .en(t23), .clk(Clock_in), .Q(o23));  // open: clr
  Register #(.width(32)) register_24 (.D(WData), .en(t24), .clk(Clock_in), .Q(o24));  // open: clr
  Register #(.width(32)) register_25 (.D(WData), .en(t25), .clk(Clock_in), .Q(o25));  // open: clr
  Register #(.width(32)) register_26 (.D(WData), .en(t26), .clk(Clock_in), .Q(o26));  // open: clr
  Register #(.width(32)) register_27 (.D(WData), .en(t27), .clk(Clock_in), .Q(o27));  // open: clr
  Register #(.width(32)) register_28 (.D(WData), .en(t28), .clk(Clock_in), .Q(o28));  // open: clr
  Register #(.width(32)) register_29 (.D(WData), .en(t29), .clk(Clock_in), .Q(o29));  // open: clr
  Register #(.width(32)) register_30 (.D(WData), .en(t30), .clk(Clock_in), .Q(o30));  // open: clr
  Register #(.width(32)) register_31 (.D(WData), .en(t31), .clk(Clock_in), .Q(o31));  // open: clr
  Register #(.width(32)) register_32 (.D(WData), .en(t32), .clk(Clock_in), .Q(o32));  // open: clr
  Multiplexer #(.enable("false"), .select(5), .width(32)) multiplexer_1 (
    .in0(o1), .in1(o2), .in2(o31), .in3(o3), .in4(o4), .in5(o5), .in6(o6), .in7(o7), .in8(o8), .in9(o9),
    .in10(o10), .in11(o11), .in12(o12), .in13(o13), .in14(o14), .in15(o15), .in16(o16), .in17(o17),
    .in18(o18), .in19(o19), .in20(o20), .in21(o21), .in22(o22), .in23(o23), .in24(o24), .in25(o25),
    .in26(o26), .in27(o27), .in28(o28), .in29(o29), .in30(o30), .in31(o32), .out(RData), .sel(RReg1));
  Multiplexer #(.enable("false"), .select(5), .width(32)) multiplexer_2 (
    .in0(o1), .in1(o2), .in2(o31), .in3(o3), .in4(o4), .in5(o5), .in6(o6), .in7(o7), .in8(o8), .in9(o9),
    .in10(o10), .in11(o11), .in12(o12), .in13(o13), .in14(o14), .in15(o15), .in16(o16), .in17(o17),
    .in18(o18), .in19(o19), .in20(o20), .in21(o21), .in22(o22), .in23(o23), .in24(o24), .in25(o25),
    .in26(o26), .in27(o27), .in28(o28), .in29(o29), .in30(o30), .in31(o32), .out(RData2), .sel(RReg2));

  // Other names for the same wires on the sheet: Clk = Clock_in; WD[31:0] = WData; WT = Write
endmodule
