// Logisim project Lab5.circ as structural Verilog: 13 circuits, main circuit main
module main (
  input  [31:0] in_1
);

  wire alu_control_1_alu_src, and_1_out, clock_1_out, comparator_1_eq, control_1_branch, control_1_memread,
       control_1_memtoreg, control_1_memwrite, control_1_regwrite, undriven, undriven_2;
  wire [3:0] alu_control_1_alu_ctrl0;
  wire [31:0] adder_1_out, adder_2_out, alu_32_1_result, dram16m32_1_out_6, immgen_1_imm32,
       instructionamemory_1_instruction, multiplexer_1_out, multiplexer_2_out, multiplexer_3_out,
       regisger_files_1_rdata1, regisger_files_1_rdata2, register_1_q;

  Register #(.width(32)) register_1 (
    .D(multiplexer_2_out), .en(1'b1), .clk(clock_1_out), .Q(register_1_q));  // open: clr
  Clock clock_1 (.out(clock_1_out));
  InstructionaMemory instructionamemory_1 (
    .Address(register_1_q), .ClockIn(clock_1_out), .Instruction(instructionamemory_1_instruction));
  Adder #(.width(32)) adder_1 (.a(register_1_q), .b(in_1), .out(adder_1_out));  // open: cin, cout
  ImmGen immgen_1 (.Instruction(instructionamemory_1_instruction), .Imm32(immgen_1_imm32));
  Control control_1 (
    .I6(instructionamemory_1_instruction[0]), .I5(instructionamemory_1_instruction[1]),
    .I4(instructionamemory_1_instruction[2]), .I3(instructionamemory_1_instruction[3]),
    .I2(instructionamemory_1_instruction[4]), .I1(instructionamemory_1_instruction[5]),
    .I0(instructionamemory_1_instruction[6]), .MemToReg(control_1_memtoreg), .RegWrite(control_1_regwrite),
    .MemRead(control_1_memread), .MemWrite(control_1_memwrite), .Branch(control_1_branch));
  Regisger_files regisger_files_1 (
    .WData(multiplexer_3_out), .RReg1(instructionamemory_1_instruction[23:19]), .Clock_in(clock_1_out),
    .WReg(instructionamemory_1_instruction[15:11]), .Write(control_1_regwrite),
    .RReg2(instructionamemory_1_instruction[31:27]), .RData1(regisger_files_1_rdata1),
    .RData2(regisger_files_1_rdata2));
  ALU_Control alu_control_1 (
    .I30(instructionamemory_1_instruction[0]), .I14(instructionamemory_1_instruction[1]),
    .I13(instructionamemory_1_instruction[2]), .I12(instructionamemory_1_instruction[3]),
    .I6(instructionamemory_1_instruction[4]), .I5(undriven), .I4(undriven_2),
    .ALU_CTRL3(alu_control_1_alu_ctrl0[3]), .ALU_CTRL2(alu_control_1_alu_ctrl0[2]),
    .ALU_CTRL1(alu_control_1_alu_ctrl0[1]), .ALU_CTRL0(alu_control_1_alu_ctrl0[0]),
    .ALU_SRC(alu_control_1_alu_src));
  Multiplexer #(.enable("false"), .width(32)) multiplexer_1 (
    .in0(regisger_files_1_rdata2), .in1(immgen_1_imm32), .out(multiplexer_1_out), .sel(alu_control_1_alu_src));
  Adder #(.width(32)) adder_2 (.a(register_1_q), .b(immgen_1_imm32), .out(adder_2_out));  // open: cin, cout
  Comparator #(.width(32)) comparator_1 (
    .a(regisger_files_1_rdata1), .b(regisger_files_1_rdata2), .eq(comparator_1_eq));  // open: gt, lt
  and and_1 (and_1_out, control_1_branch, comparator_1_eq);
  ALU_32 alu_32_1 (
    .ALU_Ctrl(alu_control_1_alu_ctrl0), .A(regisger_files_1_rdata1), .B(multiplexer_1_out),
    .Result(alu_32_1_result));  // open: C_out
  Multiplexer #(.enable("false"), .width(32)) multiplexer_2 (
    .in0(adder_1_out), .in1(adder_2_out), .out(multiplexer_2_out), .sel(and_1_out));
  DRAM16M32 dram16m32_1 (
    .Address(alu_32_1_result), .MemWrite(control_1_memwrite), .MemRead(control_1_memread),
    .Clk_In(clock_1_out), .WriteData(regisger_files_1_rdata2), .out_6(dram16m32_1_out_6));
  Multiplexer #(.enable("false"), .width(32)) multiplexer_3 (
    .in0(alu_32_1_result), .in1(dram16m32_1_out_6), .out(multiplexer_3_out), .sel(control_1_memtoreg));
endmodule

module DRAM16M32 (
  input  [31:0] Address,
  input  MemWrite,
  input  MemRead,
  input  Clk_In,
  input  [31:0] WriteData,
  output [31:0] out_6
);

  RAM #(.addrWidth(24), .asyncread("true"), .dataWidth(32)) ram_1 (
    .addr(Address[25:2]), .we(MemWrite), .oe(MemRead), .clk(Clk_In), .din(WriteData), .dout(out_6));
endmodule

module ImmGen (
  input  [31:0] Instruction,
  output [31:0] Imm32
);

  Multiplexer #(.enable("false"), .width(4)) multiplexer_1 (
    .in0(Instruction[24:21]), .in1(Instruction[11:8]), .out(Imm32[4:1]), .sel(Instruction[5]));
  Multiplexer #(.enable("false")) multiplexer_2 (
    .in0(Instruction[31]), .in1(Instruction[7]), .out(Imm32[11]), .sel(Instruction[6]));
  assign Imm32[31:12] = {{19{Instruction[31]}}, Instruction[31]};  // Bit_Extender bit_extender_1
  Multiplexer #(.enable("false"), .select(2)) multiplexer_3 (
    .in0(Instruction[20]), .in1(Instruction[7]), .in3(1'b0), .out(Imm32[0]), .sel(Instruction[6:5]));  // open: in2

  assign Imm32[10:5] = Instruction[30:25];
endmodule

module Control (
  input  I6,
  input  I5,
  input  I4,
  input  I3,
  input  I2,
  input  I1,
  input  I0,
  output MemToReg,
  output RegWrite,
  output MemRead,
  output MemWrite,
  output Branch
);

  wire not_1_out, not_2_out;

  not not_1 (not_1_out, I6);
  not not_2 (not_2_out, I5);
  not not_3 (MemToReg, I4);
  or or_1 (RegWrite, not_2_out, I4);
  and and_1 (MemRead, not_2_out, MemToReg);
  and and_2 (MemWrite, not_1_out, I5, MemToReg);

  assign Branch = I6;
endmodule

module FullAdder (
  input  A,
  input  B,
  input  C_in,
  output Sum,
  output Cout
);

  wire and_1_out, and_2_out, and_3_out, and_4_out, and_5_out, and_6_out, and_7_out, not_1_out, not_2_out,
       not_3_out;

  not not_1 (not_1_out, A);
  not not_2 (not_2_out, B);
  not not_3 (not_3_out, C_in);
  and and_1 (and_1_out, not_1_out, not_2_out, C_in);
  and and_2 (and_2_out, not_1_out, B, not_3_out);
  and and_3 (and_3_out, A, not_3_out, not_2_out);
  and and_4 (and_4_out, A, B, C_in);
  and and_5 (and_5_out, B, C_in);
  and and_6 (and_6_out, A, C_in);
  and and_7 (and_7_out, A, B);
  or or_1 (Sum, and_1_out, and_2_out, and_3_out, and_4_out);
  or or_2 (Cout, and_5_out, and_6_out, and_7_out);
endmodule

module ALU (
  input  [3:0] ALU_Ctrl,
  input  A,
  input  B,
  input  C_in,
  output R,
  output C_out
);

  wire and_1_out, fulladder_1_sum, multiplexer_1_out, not_1_out, or_1_out, xor_1_out;

  not not_1 (not_1_out, B);
  Multiplexer #(.enable("false")) multiplexer_1 (.in0(B), .in1(not_1_out), .out(multiplexer_1_out), .sel(ALU_Ctrl[2]));
  and and_1 (and_1_out, A, multiplexer_1_out);
  or or_1 (or_1_out, A, multiplexer_1_out);
  xor xor_1 (xor_1_out, A, multiplexer_1_out);
  FullAdder fulladder_1 (.A(A), .B(multiplexer_1_out), .C_in(C_in), .Sum(fulladder_1_sum), .Cout(C_out));
  Multiplexer #(.enable("false"), .select(2)) multiplexer_2 (
    .in0(and_1_out), .in1(or_1_out), .in2(xor_1_out), .in3(fulladder_1_sum), .out(R), .sel(ALU_Ctrl[1:0]));
endmodule

module ALU_4 (
  input  [3:0] ALU_Ctrl,
  input  C_in,
  input  [3:0] A,
  input  [3:0] B,
  output [3:0] S,
  output C_out
);

  wire alu_1_c_out, alu_2_c_out, alu_3_c_out;

  ALU alu_1 (.ALU_Ctrl(ALU_Ctrl), .A(A[0]), .B(B[0]), .C_in(C_in), .R(S[0]), .C_out(alu_1_c_out));
  ALU alu_2 (.ALU_Ctrl(ALU_Ctrl), .A(A[1]), .B(B[1]), .C_in(alu_1_c_out), .R(S[1]), .C_out(alu_2_c_out));
  ALU alu_3 (.ALU_Ctrl(ALU_Ctrl), .A(A[2]), .B(B[2]), .C_in(alu_2_c_out), .R(S[2]), .C_out(alu_3_c_out));
  ALU alu_4 (.ALU_Ctrl(ALU_Ctrl), .A(A[3]), .B(B[3]), .C_in(alu_3_c_out), .R(S[3]), .C_out(C_out));
endmodule

module ALU_32 (
  input  [3:0] ALU_Ctrl,
  input  [31:0] A,
  input  [31:0] B,
  output [31:0] Result,
  output C_out
);

  wire alu_4_1_c_out, alu_4_2_c_out, alu_4_3_c_out, alu_4_4_c_out, alu_4_5_c_out, alu_4_6_c_out,
       alu_4_7_c_out;

  ALU_4 alu_4_1 (
    .ALU_Ctrl(ALU_Ctrl), .C_in(ALU_Ctrl[2]), .A(A[3:0]), .B(B[3:0]), .S(Result[3:0]), .C_out(alu_4_1_c_out));
  ALU_4 alu_4_2 (
    .ALU_Ctrl(ALU_Ctrl), .C_in(alu_4_1_c_out), .A(A[7:4]), .B(B[7:4]), .S(Result[7:4]), .C_out(alu_4_2_c_out));
  ALU_4 alu_4_3 (
    .ALU_Ctrl(ALU_Ctrl), .C_in(alu_4_2_c_out), .A(A[11:8]), .B(B[11:8]), .S(Result[11:8]),
    .C_out(alu_4_3_c_out));
  ALU_4 alu_4_4 (
    .ALU_Ctrl(ALU_Ctrl), .C_in(alu_4_3_c_out), .A(A[15:12]), .B(B[15:12]), .S(Result[15:12]),
    .C_out(alu_4_4_c_out));
  ALU_4 alu_4_5 (
    .ALU_Ctrl(ALU_Ctrl), .C_in(alu_4_4_c_out), .A(A[19:16]), .B(B[23:20]), .S(Result[19:16]),
    .C_out(alu_4_5_c_out));
  ALU_4 alu_4_6 (
    .ALU_Ctrl(ALU_Ctrl), .C_in(alu_4_5_c_out), .A(A[23:20]), .B(B[23:20]), .S(Result[23:20]),
    .C_out(alu_4_6_c_out));
  ALU_4 alu_4_7 (
    .ALU_Ctrl(ALU_Ctrl), .C_in(alu_4_6_c_out), .A(A[27:24]), .B(B[27:24]), .S(Result[27:24]),
    .C_out(alu_4_7_c_out));
  ALU_4 alu_4_8 (
    .ALU_Ctrl(ALU_Ctrl), .C_in(alu_4_7_c_out), .A(A[31:28]), .B(B[31:28]), .S(Result[31:28]), .C_out(C_out));

  assign B[19:16] = B[23:20];
endmodule

module ALU_Control (
  input  I30,
  input  I14,
  input  I13,
  input  I12,
  input  I6,
  input  I5,
  input  I4,
  output ALU_CTRL3,
  output ALU_CTRL2,
  output ALU_CTRL1,
  output ALU_CTRL0,
  output ALU_SRC
);

  wire nand_1_out, nand_2_out, nand_4_out, nand_7_out;

  nand nand_1 (nand_1_out, I30, I5);
  nand nand_2 (nand_2_out, I30, I5);
  nand nand_3 (ALU_CTRL1, I13, I4);
  nand nand_4 (nand_4_out, 1'b1, I12);
  nand nand_5 (ALU_SRC, I5, I4);
  nand nand_6 (ALU_CTRL2, nand_1_out, nand_2_out);
  nand nand_7 (nand_7_out, I13, nand_4_out);
  nand nand_8 (ALU_CTRL0, I14, nand_7_out);

  assign ALU_CTRL3 = 1'b0;
endmodule

module Regisger_files (
  input  [31:0] WData,
  input  [4:0] RReg1,
  input  Clock_in,
  input  [4:0] WReg,
  input  Write,
  input  [4:0] RReg2,
  output [31:0] RData1,
  output [31:0] RData2
);

  wire t1, t2, t3, t4, t5, t6, t7, t8, t9, t10, t11, t12, t13, t14, t15, t16, t17, t18, t19, t20, t21, t22,
       t23, t24, t25, t26, t27, t28, t29, t30, t31, t32;
  wire [31:0] o1, o2, o3, o4, o5, o6, o7, o8, o9, o10, o11, o12, o13, o14, o15, o16, o17, o18, o19, o20, o21,
       o22, o23, o24, o25, o26, o27, o28, o29, o30, o31, o32;

  Demultiplexer #(.enable("false"), .select(5)) demultiplexer_1 (
    .out0(t1), .out1(t2), .out2(t3), .out3(t4), .out4(t5), .out5(t6), .out6(t7), .out7(t8), .out8(t9),
    .out9(t10), .out10(t11), .out11(t12), .out12(t13), .out13(t14), .out14(t15), .out15(t16), .out16(t17),
    .out17(t18), .out18(t19), .out19(t20), .out20(t21), .out21(t22), .out22(t23), .out23(t24), .out24(t25),
    .out25(t26), .out26(t27), .out27(t28), .out28(t29), .out29(t30), .out30(t31), .out31(t32), .in(Write),
    .sel(WReg));
  Register #(.width(32)) register_1 (.D(WData), .en(t1), .clk(Clock_in), .Q(o1), .clr(Write));
  Register #(.width(32)) register_2 (.D(WData), .en(t2), .clk(Clock_in), .Q(o2));  // open: clr
  Register #(.width(32)) register_3 (.D(WData), .en(t3), .clk(Clock_in), .Q(o3));  // open: clr
  Register #(.width(32)) register_4 (.D(WData), .en(t4), .clk(Clock_in), .Q(o4));  // open: clr
  Register #(.width(32)) register_5 (.D(WData), .en(t5), .clk(Clock_in), .Q(o5));  // open: clr
  Register #(.width(32)) register_6 (.D(WData), .en(t6), .clk(Clock_in), .Q(o6));  // open: clr
  Register #(.width(32)) register_7 (.D(WData), .en(t7), .clk(Clock_in), .Q(o7));  // open: clr
  Register #(.width(32)) register_8 (.D(WData), .en(t8), .clk(Clock_in), .Q(o8));  // open: clr
  Register #(.width(32)) register_9 (.D(WData), .en(t9), .clk(Clock_in), .Q(o9));  // open: clr
  Register #(.width(32)) register_10 (.D(WData), .en(t10), .clk(Clock_in), .Q(o10));  // open: clr
  Register #(.width(32)) register_11 (.D(WData), .en(t11), .clk(Clock_in), .Q(o11));  // open: clr
  Register #(.width(32)) register_12 (.D(WData), .en(t12), .clk(Clock_in), .Q(o12));  // open: clr
  Register #(.width(32)) register_13 (.D(WData), .en(t13), .clk(Clock_in), .Q(o13));  // open: clr
  Register #(.width(32)) register_14 (.D(WData), .en(t14), .clk(Clock_in), .Q(o14));  // open: clr
  Register #(.width(32)) register_15 (.D(WData), .en(t15), .clk(Clock_in), .Q(o15));  // open: clr
  Register #(.width(32)) register_16 (.D(WData), .en(t16), .clk(Clock_in), .Q(o16));  // open: clr
  Register #(.width(32)) register_17 (.D(WData), .en(t17), .clk(Clock_in), .Q(o17));  // open: clr
  Register #(.width(32)) register_18 (.D(WData), .en(t18), .clk(Clock_in), .Q(o18));  // open: clr
  Register #(.width(32)) register_19 (.D(WData), .en(t19), .clk(Clock_in), .Q(o19));  // open: clr
  Register #(.width(32)) register_20 (.D(WData), .en(t20), .clk(Clock_in), .Q(o20));  // open: clr
  Register #(.width(32)) register_21 (.D(WData), .en(t21), .clk(Clock_in), .Q(o21));  // open: clr
  Register #(.width(32)) register_22 (.D(WData), .en(t22), .clk(Clock_in), .Q(o22));  // open: clr
  Register #(.width(32)) register_23 (.D(WData), .en(t23), .clk(Clock_in), .Q(o23));  // open: clr
  Register #(.width(32)) register_24 (.D(WData), .en(t24), .clk(Clock_in), .Q(o24));  // open: clr
  Register #(.width(32)) register_25 (.D(WData), .en(t25), .clk(Clock_in), .Q(o25));  // open: clr
  Register #(.width(32)) register_26 (.D(WData), .en(t26), .clk(Clock_in), .Q(o26));  // open: clr
  Register #(.width(32)) register_27 (.D(WData), .en(t27), .clk(Clock_in), .Q(o27));  // open: clr
  Register #(.width(32)) register_28 (.D(WData), .en(t28), .clk(Clock_in), .Q(o28));  // open: clr
  Register #(.width(32)) register_29 (.D(WData), .en(t29), .clk(Clock_in), .Q(o29));  // open: clr
  Register #(.width(32)) register_30 (.D(WData), .en(t30), .clk(Clock_in), .Q(o30));  // open: clr
  Register #(.width(32)) register_31 (.D(WData), .en(t31), .clk(Clock_in), .Q(o31));  // open: clr
  Register #(.width(32)) register_32 (.D(WData), .en(t32), .clk(Clock_in), .Q(o32));  // open: clr
  Multiplexer #(.enable("false"), .select(5), .width(32)) multiplexer_1 (
    .in0(o1), .in1(o2), .in2(o3), .in3(o4), .in4(o5), .in5(o6), .in6(o7), .in7(o8), .in8(o9), .in9(o10),
    .in10(o11), .in11(o12), .in12(o13), .in13(o14), .in14(o15), .in15(o16), .in16(o17), .in17(o18),
    .in18(o19), .in19(o20), .in20(o21), .in21(o22), .in22(o23), .in23(o24), .in24(o25), .in25(o26),
    .in26(o27), .in27(o28), .in28(o29), .in29(o30), .in30(o31), .in31(o32), .out(RData1), .sel(RReg1));
  Multiplexer #(.enable("false"), .select(5), .width(32)) multiplexer_2 (
    .in0(o1), .in1(o2), .in2(o3), .in3(o4), .in4(o5), .in5(o6), .in6(o7), .in7(o8), .in8(o9), .in9(o10),
    .in10(o11), .in11(o12), .in12(o13), .in13(o14), .in14(o15), .in15(o16), .in16(o17), .in17(o18),
    .in18(o19), .in19(o20), .in20(o21), .in21(o22), .in22(o23), .in23(o24), .in24(o25), .in25(o26),
    .in26(o27), .in27(o28), .in28(o29), .in29(o30), .in30(o31), .in31(o32), .out(RData2), .sel(RReg2));

  // Other names for the same wires on the sheet: Clk = Clock_in; WD[31:0] = WData; WT = Write
endmodule

module RV32_Digital_Circuit (
  input  [31:0] Instruction
);

  wire alu_control_1_alu_src, clock_1_out;
  wire [3:0] alu_control_1_alu_ctrl0;
  wire [31:0] alu_32_1_result, bit_extender_1_out, multiplexer_1_out, regisger_files_1_rdata1,
       regisger_files_1_rdata2;

  Clock clock_1 (.out(clock_1_out));
  assign bit_extender_1_out = {{20{1'b0}}, Instruction[31:20]};  // Bit_Extender bit_extender_1
  Regisger_files regisger_files_1 (
    .WData(alu_32_1_result), .RReg1(Instruction[19:15]), .Clock_in(clock_1_out), .WReg(Instruction[11:7]),
    .Write(1'b1), .RReg2(Instruction[24:20]), .RData1(regisger_files_1_rdata1),
    .RData2(regisger_files_1_rdata2));
  ALU_Control alu_control_1 (
    .I30(Instruction[30]), .I14(Instruction[14]), .I13(Instruction[13]), .I12(Instruction[12]),
    .I6(Instruction[6]), .I5(Instruction[5]), .I4(Instruction[4]), .ALU_CTRL3(alu_control_1_alu_ctrl0[3]),
    .ALU_CTRL2(alu_control_1_alu_ctrl0[2]), .ALU_CTRL1(alu_control_1_alu_ctrl0[1]),
    .ALU_CTRL0(alu_control_1_alu_ctrl0[0]), .ALU_SRC(alu_control_1_alu_src));
  Multiplexer #(.enable("false"), .width(32)) multiplexer_1 (
    .in0(regisger_files_1_rdata2), .in1(bit_extender_1_out), .out(multiplexer_1_out),
    .sel(alu_control_1_alu_src));
  ALU_32 alu_32_1 (
    .ALU_Ctrl(alu_control_1_alu_ctrl0), .A(regisger_files_1_rdata1), .B(multiplexer_1_out),
    .Result(alu_32_1_result));  // open: C_out
endmodule

module InstructionaMemory (
  input  [31:0] Address,
  input  ClockIn,
  output [31:0] Instruction
);

  wire not_1_out;

  not not_1 (not_1_out, ClockIn);
  RAM #(.addrWidth(22), .asyncread("true"), .dataWidth(32)) ram_1 (
    .addr(Address[23:2]), .we(1'b0), .oe(not_1_out), .dout(Instruction));  // open: clk, din
endmodule

module Shitf32 (
  input  [3:0] ALU_Ctrl,
  input  [31:0] A,
  input  [31:0] B,
  output [31:0] Result,
  output C_out
);

  wire [31:0] alu_32_1_result, multiplexer_1_out, shifter_1_out, shifter_2_out, shifter_3_out;

  Shifter #(.width(32)) shifter_1 (.in(A), .\dist (B[4:0]), .out(shifter_1_out));
  Shifter #(.shift("lr"), .width(32)) shifter_2 (.in(A), .\dist (B[4:0]), .out(shifter_2_out));
  Shifter #(.width(32)) shifter_3 (.in(A), .\dist (B[4:0]), .out(shifter_3_out));
  Multiplexer #(.enable("false"), .select(2), .width(32)) multiplexer_1 (
    .in0(shifter_1_out), .in1(shifter_2_out), .in2(shifter_3_out), .out(multiplexer_1_out),
    .sel(ALU_Ctrl[1:0]));  // open: in3
  ALU_32 alu_32_1 (.ALU_Ctrl(ALU_Ctrl), .A(A), .B(B), .Result(alu_32_1_result), .C_out(C_out));
  Multiplexer #(.enable("false"), .width(32)) multiplexer_2 (
    .in0(alu_32_1_result), .in1(multiplexer_1_out), .out(Result), .sel(ALU_Ctrl[2]));
endmodule
